# Fritzing sketch ArduinoAsISP (saved by Fritzing 0.9.3b)

parts:
  Pro_Micro1 = Pro Micro
  元件1 = Arduino Uno (Rev3)

nets:
  N1: Pro_Micro1.D16/MOSI, 元件1.D11_PWM/MOSI
  N2: Pro_Micro1.D14/MISO, 元件1.D12/MISO
  N3: Pro_Micro1.D15/SCLK, 元件1.D13/SCK
  N4: Pro_Micro1.RST, 元件1.D10_PWM/SS
  GND: Pro_Micro1.GND, 元件1.GND
  N5: Pro_Micro1.RAW, 元件1.5V

custom parts:
  Pro Micro: The SparkFun Pro Micro is a complete USB-based microcontoller development system, in a very small footprint, capable of implementing many types of projects. All programming can be done via the USB port.
